# Fritzing sketch LEDStrip (saved by Fritzing 0.9.4)
breadboards: 2

parts:
  12V_Input = Power plug
  1kΩ = Resistor [tolerance=±1% resistance=1k package=THT]
  220Ω = Resistor [tolerance=±5% resistance=220 package=THT]
  220µF = Electrolytic Capacitor [capacitance=220µF voltage=20V package="100 mil [THT, electrolytic]"]
  200kΩ = Resistor [tolerance=±1% resistance=200k package=THT]
  2kΩ = Resistor [tolerance=±1% resistance=2k package=THT]
  330Ω = Resistor [tolerance=±1% resistance=330 package=THT]
  470µF = Electrolytic Capacitor [capacitance=470µF voltage=20V package="100 mil [THT, electrolytic]"]
  M1 = ESP32-S2-DevKitC-1 [part_number=ESP32-S2-DevKitC-1]
  LED_Strip_Addressable = female pin header, 3 pins [form="♀ (female)"]
  LCD = female pin header, 4 pins [form="♀ (female)"]
  3_3V = female pin header, 2 pins [form="♀ (female)"]
  5v = female pin header, 2 pins [form="♀ (female)"]
  12V = female pin header, 2 pins [form="♀ (female)"]
  Schottky = Rectifier Diode [package="Melf DO-213 AA [SMD]"]
  33uH = Inductors [package=cr54]
  220µF_2 = Electrolytic Capacitor [capacitance=220µF voltage=20V package="100 mil [THT, electrolytic]"]
  Mic = female pin header, 5 pins [form="♀ (female)"]
  Schottky_2 = Rectifier Diode [package="Melf DO-213 AA [SMD]"]
  220µF_3 = Electrolytic Capacitor [capacitance=220µF package="100 mil [THT, electrolytic]"]
  220µF_4 = Electrolytic Capacitor [capacitance=220µF package="100 mil [THT, electrolytic]"]
  470µF_2 = Electrolytic Capacitor [capacitance=470µF package="100 mil [THT, electrolytic]"]
  33uH_2 = Inductors [package=cr54]
  3_3V_2 = female pin header, 2 pins [form="♀ (female)"]
  5V = female pin header, 2 pins [form="♀ (female)"]
  12V_2 = female pin header, 2 pins [form="♀ (female)"]
  MSGEQ1 = MSGEQ7 [chip_label=IC package="DIP (Dual Inline) [THT]"]
  LM2596_2 = LM2596 [package=q5-dd_spx29300]
  33pF = Capacitor [package=0603-cap]
  100nF = Capacitor [package=0603-cap]
  10nF = Capacitor [package=0603-cap]
  100nF_2 = Capacitor [package=0603-cap]
  20kΩ = Resistor [tolerance=±1% resistance=20k package=THT]
  Gain = Solder Jumper [package=sj_3_paste1_2]
  MOSFET_B = MOSFET-NCHANNEL [package=sot23-3]
  MOSFET_R = MOSFET-NCHANNEL [package=sot23-3]
  MOSFET_G = MOSFET-NCHANNEL [package=sot23-3]
  LED_Strip = female pin header, 4 pins [form="♀ (female)"]
  LED_Matrix = female pin header, 5 pins [form="♀ (female)"]
  Pot_BK = female pin header, 3 pins [form="♀ (female)"]
  Gain_Pot = female pin header, 3 pins [form="♀ (female)"]
  BK = JUMPER-3 [package=sj_3_paste2_3]
  Button = female pin header, 4 pins [form="♀ (female)"]
  LM2596_1 = LM2596 [package=q5-dd_spx29300]

nets:
  GND: 12V_Input.GND, 1kΩ.Pin_1, 220Ω.Pin_0, 220µF.-, 470µF.-, M1.pin_22, M1.pin_23, M1.pin_24, M1.pin_44, LED_Strip_Addressable.pin3, 3_3V.pin1, 5v.pin1, 12V.pin1, Schottky.anode, 220µF_2.-, Mic.pin5, Schottky_2.anode, 220µF_3.-, 220µF_4.-, 470µF_2.-, 3_3V_2.pin1, 12V_2.pin1, LM2596_2.GND, LM2596_2.On/Off, 33pF.2, 100nF.1, Gain.1, Pot_BK.pin1, Gain_Pot.pin1, BK.1, LM2596_1.GND, LM2596_1.On/Off
  VIN: 12V_Input.VCC, 220µF.+, 470µF.+, 12V.pin2, 220µF_3.+, 470µF_2.+, 12V_2.pin2, LM2596_2.VIN, LED_Strip.pin4, LM2596_1.VIN
  N1: 1kΩ.Pin_0, M1.pin_4, Button.pin1
  N2: 220Ω.Pin_1, Button.pin4
  N3: 200kΩ.Pin_0, M1.pin_21, 33uH.2, 220µF_2.+, MSGEQ1.VDD, 100nF_2.2, LM2596_1.Feedback
  N4: 200kΩ.Pin_1, MSGEQ1.CKIN, 33pF.1
  N5: 2kΩ.Pin_0, 10nF.2
  N6: 2kΩ.Pin_1, 20kΩ.Pin_0
  N7: 330Ω.Pin_0, M1.pin_39
  N8: 330Ω.Pin_1, LED_Strip_Addressable.pin2
  N9: M1.pin_1, M1.pin_2, LCD.pin1, 3_3V.pin2, Mic.pin4, 3_3V_2.pin2, Gain.3, Pot_BK.pin3, Gain_Pot.pin3, BK.3, Button.pin2, Button.pin3
  N10: M1.pin_5, MSGEQ1.GND
  N11: M1.pin_11, LCD.pin3
  N12: M1.pin_15, LCD.pin2
  N13: M1.pin_28, LED_Matrix.pin2
  N14: M1.pin_29, LED_Matrix.pin1
  N15: M1.pin_30, LED_Matrix.pin3
  N16: M1.pin_36, MOSFET_B.G
  N17: M1.pin_37, MOSFET_R.G
  N18: M1.pin_38, MOSFET_G.G
  N19: M1.pin_40, MSGEQ1.STROBE
  N20: M1.pin_41, MSGEQ1.OUT
  N21: LED_Strip_Addressable.pin1, 5v.pin2
  N22: Schottky.cathode, 33uH.1, LM2596_1.OUT
  N23: Mic.pin2, 20kΩ.Pin_1
  N24: Mic.pin3, Gain.2, Gain_Pot.pin2
  N25: Schottky_2.cathode, 33uH_2.1, LM2596_2.OUT
  N26: 220µF_4.+, 33uH_2.2, 5V.pin2, LM2596_2.Feedback, LED_Matrix.pin5
  N27: 5V.pin1, MSGEQ1.VSS, 100nF_2.1, MOSFET_B.S, MOSFET_R.S, MOSFET_G.S, LED_Matrix.pin4
  N28: MSGEQ1.IN, 10nF.1
  N29: MSGEQ1.pin6, 100nF.2
  N30: MOSFET_B.D, LED_Strip.pin1
  N31: MOSFET_R.D, LED_Strip.pin2
  N32: MOSFET_G.D, LED_Strip.pin3
  N33: Pot_BK.pin2, BK.2

notes:
  Note that the ESP32 board below is ESP32 S2. I'm actually using ESP32 S3 so I'm keeping the pin LOCATION constant and ignoring the pin NUMBERS for the bottom rail which differ between S2 and S3.

custom parts:
  ESP32-S2-DevKitC-1: ESP32-S2-DevKitC-1 is an entry-level development board based on ESP32-S2-SOLO (on-board PCB antenna). It is based on the ESP32 microcontroller that boasts Wifi, Bluetooth, Ethernet and Low Power support all in a single chip. (vanepp) Feb 2022: converted to ESP32-S2-DevKitC-1. This module is 44pins long (2x22) and 11 pins width.
  MSGEQ7: A DIP stand-in part for whatever IC you want. With 8 pins on a 300mil dual inline package (DIP) footprint.
  LM2596: LM2596 SIMPLE SWITCHER® Power Converter 150-kHz 3-A Step-Down Voltage Regulator
